// Logisim project 1x4demux.circ as structural Verilog: 1 circuit, main circuit main
module main (
  input  D,
  input  S1,
  input  S0
);

  wire nand_1_out, nand_2_out, nand_3_out, nand_4_out, nand_5_out, nand_6_out, nand_7_out, nand_8_out,
       nand_9_out, nand_10_out, nand_11_out, nand_12_out, nand_13_out, nand_14_out, nand_15_out, nand_16_out,
       nand_17_out, nand_18_out;

  nand nand_1 (nand_1_out, S1, S1);
  nand nand_2 (nand_2_out, S0, S0);
  nand nand_3 (nand_3_out, nand_2_out, nand_1_out);
  nand nand_4 (nand_4_out, S0, nand_1_out);
  nand nand_5 (nand_5_out, nand_2_out, S1);
  nand nand_6 (nand_6_out, S0, S1);
  nand nand_7 (nand_7_out, nand_3_out, nand_3_out);
  nand nand_8 (nand_8_out, nand_4_out, nand_4_out);
  nand nand_9 (nand_9_out, nand_5_out, nand_5_out);
  nand nand_10 (nand_10_out, nand_6_out, nand_6_out);
  nand nand_11 (nand_11_out, nand_7_out, D);
  nand nand_12 (nand_12_out, nand_8_out, D);
  nand nand_13 (nand_13_out, nand_9_out, D);
  nand nand_14 (nand_14_out, nand_10_out, D);
  nand nand_15 (nand_15_out, nand_11_out, nand_11_out);
  LED led_1 (.in(nand_15_out));
  nand nand_16 (nand_16_out, nand_12_out, nand_12_out);
  LED led_2 (.in(nand_16_out));
  nand nand_17 (nand_17_out, nand_13_out, nand_13_out);
  LED led_3 (.in(nand_17_out));
  nand nand_18 (nand_18_out, nand_14_out, nand_14_out);
  LED led_4 (.in(nand_18_out));

  // Notes on the sheet:
  //   S1'
  //   S0'
  //   (S1'S0')'
  //   (S1'S0)'
  //   (S1S0')'
  //   (S1S0)'
  //   (S1'S0'D)'
  //   (S1'S0D)'
  //   (S1S0'D)'
  //   (S1S0D)'
  //   Y0=S1'S0'D
  //   Y1=S1'S0D
  //   Y2=S1S0'D
  //   Y3=S1S0D
endmodule
