// Logisim project Experiment-4_Multiplexer.circ as structural Verilog: 1 circuit, main circuit main
module main (
  input  I3,
  input  I2,
  input  I1,
  input  I0,
  input  S1,
  input  S0
);

  wire nand_1_out, nand_2_out, nand_3_out, nand_4_out, nand_5_out, nand_6_out, nand_7_out, nand_8_out,
       nand_9_out, nand_10_out, nand_11_out;

  nand nand_1 (nand_1_out, S0, S0);
  nand nand_2 (nand_2_out, I3, S0);
  nand nand_3 (nand_3_out, I2, nand_1_out);
  nand nand_4 (nand_4_out, I1, S0);
  nand nand_5 (nand_5_out, I0, nand_1_out);
  nand nand_6 (nand_6_out, nand_4_out, nand_5_out);
  nand nand_7 (nand_7_out, nand_2_out, nand_3_out);
  nand nand_8 (nand_8_out, nand_7_out, S1);
  nand nand_9 (nand_9_out, S1, S1);
  nand nand_10 (nand_10_out, nand_6_out, nand_9_out);
  nand nand_11 (nand_11_out, nand_8_out, nand_10_out);
  LED led_1 (.in(nand_11_out));
endmodule
