// Logisim project down_counter.circ as structural Verilog: 1 circuit, main circuit main
module main (
);

  wire clock_1_out, nand_1_out, nand_2_out, nand_3_out, nand_4_out, nand_5_out, nand_6_out, nand_7_out,
       nand_8_out, nand_9_out, nand_10_out, nand_11_out, nand_12_out, t_ff_1_q, t_ff_1_qn, t_ff_2_q,
       t_ff_2_qn, t_ff_3_q, t_ff_3_qn, t_ff_4_q, t_ff_4_qn;

  Clock clock_1 (.out(clock_1_out));
  nand nand_1 (nand_1_out, nand_2_out, nand_4_out);
  nand nand_2 (nand_2_out, nand_3_out, nand_3_out);
  LED A (.in(t_ff_1_q));
  T_Flip_Flop t_ff_1 (
    .T(nand_1_out), .clk(clock_1_out), .Q(t_ff_1_q), .Qn(t_ff_1_qn), .reset(nand_12_out), .preset(1'b1));
  nand nand_3 (nand_3_out, t_ff_1_qn, t_ff_2_qn);
  nand nand_4 (nand_4_out, nand_5_out, nand_5_out);
  T_Flip_Flop t_ff_2 (
    .T(t_ff_1_qn), .clk(clock_1_out), .Q(t_ff_2_q), .Qn(t_ff_2_qn), .reset(nand_12_out), .preset(1'b1));
  nand nand_5 (nand_5_out, t_ff_3_qn, t_ff_4_qn);
  LED B (.in(t_ff_2_q));
  nand nand_6 (nand_6_out, nand_5_out, nand_2_out);
  nand nand_7 (nand_7_out, nand_6_out, nand_6_out);
  T_Flip_Flop t_ff_3 (
    .T(nand_7_out), .clk(clock_1_out), .Q(t_ff_3_q), .Qn(t_ff_3_qn), .reset(nand_12_out), .preset(1'b1));
  LED C (.in(t_ff_3_q));
  T_Flip_Flop t_ff_4 (
    .T(nand_9_out), .clk(clock_1_out), .Q(t_ff_4_q), .Qn(t_ff_4_qn), .reset(nand_12_out), .preset(1'b1));
  nand nand_8 (nand_8_out, t_ff_3_qn, nand_2_out);
  LED D (.in(t_ff_4_q));
  nand nand_9 (nand_9_out, nand_8_out, nand_8_out);
  nand nand_10 (nand_10_out, t_ff_1_q, t_ff_2_q);
  nand nand_11 (nand_11_out, nand_10_out, nand_10_out);
  nand nand_12 (nand_12_out, nand_11_out, t_ff_4_q);
endmodule
