// Logisim project t_ff.circ as structural Verilog: 1 circuit, main circuit main
module main (
  input  T
);

  wire CLK_out, nand_1_out, nand_2_out, nand_3_out, nand_4_out, nand_5_out, nand_6_out, nand_7_out,
       nand_8_out;

  Clock CLK (.out(CLK_out));
  nand nand_1 (nand_1_out, T, CLK_out);
  nand nand_2 (nand_2_out, CLK_out, T);
  nand nand_3 (nand_3_out, nand_1_out, nand_1_out);
  nand nand_4 (nand_4_out, nand_2_out, nand_2_out);
  nand nand_5 (nand_5_out, nand_8_out, nand_3_out);
  nand nand_6 (nand_6_out, nand_4_out, nand_7_out);
  nand nand_7 (nand_7_out, nand_5_out, nand_8_out);
  nand nand_8 (nand_8_out, nand_7_out, nand_6_out);

  // Notes on the sheet:
  //   Q
  //   Q'
endmodule
