// Logisim project test.circ as structural Verilog: 1 circuit, main circuit main
module main (
);

  wire and_1_out, and_2_out, and_3_out, clock_1_out, j_k_ff_1_q, j_k_ff_2_q, j_k_ff_3_q, j_k_ff_4_q,
       nand_1_out, not_1_out;

  Clock clock_1 (.out(clock_1_out));
  J_K_Flip_Flop j_k_ff_1 (
    .J(1'b1), .K(clock_1_out), .clk(1'b1), .Q(j_k_ff_1_q), .reset(nand_1_out));  // open: Qn, preset
  and and_1 (and_1_out, clock_1_out, j_k_ff_1_q);
  J_K_Flip_Flop j_k_ff_2 (.J(1'b1), .K(and_1_out), .clk(1'b1), .Q(j_k_ff_2_q), .reset(nand_1_out));  // open: Qn, preset
  and and_2 (and_2_out, clock_1_out, j_k_ff_2_q);
  J_K_Flip_Flop j_k_ff_3 (.J(1'b1), .K(and_2_out), .clk(1'b1), .Q(j_k_ff_3_q), .reset(nand_1_out));  // open: Qn, preset
  and and_3 (and_3_out, clock_1_out, j_k_ff_3_q);
  J_K_Flip_Flop j_k_ff_4 (.J(1'b1), .K(and_3_out), .clk(1'b1), .Q(j_k_ff_4_q), .reset(nand_1_out));  // open: Qn, preset
  nand nand_1 (nand_1_out, j_k_ff_4_q, not_1_out, j_k_ff_2_q, j_k_ff_1_q);
  not not_1 (not_1_out, j_k_ff_3_q);
endmodule
