// Logisim project test_1.circ as structural Verilog: 1 circuit, main circuit main
module main (
  input  M
);

  wire A_q, A_qn, B_q, B_qn, C_q, C_qn, clock_1_out, D_q, D_qn, nand_1_out, nand_2_out, nand_3_out,
       nand_4_out, nand_5_out, nand_6_out, nand_7_out, nand_8_out, nand_9_out, nand_10_out, nand_11_out,
       nand_12_out, nand_13_out, nand_14_out, nand_15_out, nand_16_out, nand_17_out, nand_18_out,
       nand_19_out, nand_20_out, nand_21_out, nand_22_out, nand_23_out, nand_24_out, nand_25_out,
       nand_26_out, nand_27_out, nand_28_out, nand_29_out, nand_30_out, nand_31_out, nand_32_out,
       nand_33_out, nand_34_out, nand_35_out, nand_36_out;

  Clock clock_1 (.out(clock_1_out));
  nand nand_1 (nand_1_out, M, M);
  J_K_Flip_Flop A (.J(nand_36_out), .K(1'b1), .clk(clock_1_out), .Q(A_q), .Qn(A_qn));  // open: preset, reset
  J_K_Flip_Flop B (.J(nand_8_out), .K(nand_23_out), .clk(clock_1_out), .Q(B_q), .Qn(B_qn));  // open: preset, reset
  J_K_Flip_Flop C (.J(nand_29_out), .K(nand_17_out), .clk(clock_1_out), .Q(C_q), .Qn(C_qn));  // open: preset, reset
  nand nand_2 (nand_2_out, B_qn, M);
  nand nand_3 (nand_3_out, nand_1_out, B_q);
  nand nand_4 (nand_4_out, nand_1_out, A_q);
  nand nand_5 (nand_5_out, M, A_qn);
  nand nand_6 (nand_6_out, nand_2_out, nand_2_out);
  nand nand_7 (nand_7_out, nand_3_out, nand_3_out);
  nand nand_8 (nand_8_out, nand_4_out, nand_5_out);
  nand nand_9 (nand_9_out, nand_7_out, A_q);
  nand nand_10 (nand_10_out, B_qn, C_qn);
  nand nand_11 (nand_11_out, B_q, C_q);
  nand nand_12 (nand_12_out, A_qn, nand_6_out);
  nand nand_13 (nand_13_out, nand_10_out, nand_10_out);
  nand nand_14 (nand_14_out, nand_11_out, nand_11_out);
  nand nand_15 (nand_15_out, nand_12_out, nand_3_out);
  nand nand_16 (nand_16_out, nand_12_out, nand_12_out);
  nand nand_17 (nand_17_out, nand_12_out, nand_9_out);
  nand nand_18 (nand_18_out, nand_8_out, nand_8_out);
  nand nand_19 (nand_19_out, D_qn, nand_1_out);
  nand nand_20 (nand_20_out, A_qn, nand_13_out);
  nand nand_21 (nand_21_out, A_q, nand_14_out);
  nand nand_22 (nand_22_out, D_q, nand_16_out);
  nand nand_23 (nand_23_out, D_q, nand_18_out);
  nand nand_24 (nand_24_out, C_q, nand_19_out);
  nand nand_25 (nand_25_out, nand_20_out, nand_20_out);
  nand nand_26 (nand_26_out, nand_21_out, nand_21_out);
  nand nand_27 (nand_27_out, M, nand_25_out);
  nand nand_28 (nand_28_out, nand_1_out, nand_26_out);
  nand nand_29 (nand_29_out, nand_22_out, nand_9_out);
  nand nand_30 (nand_30_out, D_q, B_qn);
  nand nand_31 (nand_31_out, B_q, M);
  nand nand_32 (nand_32_out, nand_27_out, nand_28_out);
  nand nand_33 (nand_33_out, nand_24_out, nand_24_out);
  nand nand_34 (nand_34_out, nand_30_out, nand_31_out);
  J_K_Flip_Flop D (.J(nand_32_out), .K(nand_15_out), .clk(clock_1_out), .Q(D_q), .Qn(D_qn));  // open: preset, reset
  nand nand_35 (nand_35_out, nand_34_out, nand_34_out);
  nand nand_36 (nand_36_out, nand_33_out, nand_35_out);
  LED Do (.in(D_q));
  LED Co (.in(C_q));
  LED Bo (.in(B_q));
  LED Ao (.in(A_q));
endmodule
