// Logisim project up_counter.circ as structural Verilog: 1 circuit, main circuit main
module main (
  input  in_1
);

  wire clock_1_out, clock_2_out, clock_3_out, nand_1_out, nand_2_out, nand_3_out, nand_4_out, nand_5_out,
       nand_6_out, nand_7_out, nand_8_out, nand_9_out, nand_10_out, nand_11_out, nand_12_out, nand_13_out,
       nand_14_out, nand_15_out, nand_16_out, nand_17_out, nand_18_out, nand_19_out, nand_20_out,
       nand_21_out, nand_22_out, not_1_out, not_2_out, not_3_out, t_ff_1_q, t_ff_2_q, t_ff_3_q, t_ff_4_q,
       undriven, undriven_2;

  Clock clock_1 (.out(clock_1_out));
  not not_1 (not_1_out, clock_1_out);
  Clock clock_2 (.out(clock_2_out));
  LED A (.in(t_ff_1_q));
  T_Flip_Flop t_ff_1 (.T(nand_12_out), .clk(not_1_out), .Q(t_ff_1_q), .reset(nand_21_out), .preset(in_1));  // open: Qn
  nand nand_1 (nand_1_out, undriven, clock_2_out);
  nand nand_2 (nand_2_out, clock_2_out, undriven_2);
  nand nand_3 (nand_3_out, nand_10_out, nand_1_out);
  nand nand_4 (nand_4_out, nand_2_out, nand_9_out);
  nand nand_5 (nand_5_out, nand_3_out, nand_6_out);
  nand nand_6 (nand_6_out, nand_5_out, nand_4_out);
  not not_2 (not_2_out, clock_2_out);
  Clock clock_3 (.out(clock_3_out));
  nand nand_7 (nand_7_out, nand_5_out, clock_3_out);
  nand nand_8 (nand_8_out, clock_3_out, nand_6_out);
  nand nand_9 (nand_9_out, nand_7_out, nand_10_out);
  nand nand_10 (nand_10_out, nand_9_out, nand_8_out);
  nand nand_11 (nand_11_out, t_ff_1_q, nand_12_out);
  LED B (.in(t_ff_2_q));
  T_Flip_Flop t_ff_2 (.T(nand_11_out), .clk(not_1_out), .Q(t_ff_2_q), .reset(nand_21_out));  // open: Qn, preset
  nand nand_12 (nand_12_out, t_ff_2_q, t_ff_4_q);
  nand nand_13 (nand_13_out, t_ff_1_q, t_ff_2_q);
  nand nand_14 (nand_14_out, nand_13_out, nand_13_out);
  T_Flip_Flop t_ff_3 (.T(nand_14_out), .clk(not_1_out), .Q(t_ff_3_q), .reset(nand_21_out), .preset(in_1));  // open: Qn
  LED C (.in(t_ff_3_q));
  nand nand_15 (nand_15_out, t_ff_3_q, nand_14_out);
  nand nand_16 (nand_16_out, nand_15_out, nand_12_out);
  T_Flip_Flop t_ff_4 (.T(nand_16_out), .clk(not_1_out), .Q(t_ff_4_q), .reset(nand_21_out), .preset(in_1));  // open: Qn
  LED D (.in(t_ff_4_q));
  nand nand_17 (nand_17_out, t_ff_1_q, t_ff_2_q);
  nand nand_18 (nand_18_out, nand_17_out, nand_17_out);
  not not_3 (not_3_out, t_ff_3_q);
  nand nand_19 (nand_19_out, not_3_out, t_ff_4_q);
  nand nand_20 (nand_20_out, nand_18_out, nand_22_out);
  nand nand_21 (nand_21_out, nand_20_out, nand_20_out);
  nand nand_22 (nand_22_out, nand_19_out, nand_19_out);
endmodule
